# Fritzing sketch sketch (saved by Fritzing 0.9.3b)

parts:
  R1 = Photocell (LDR) [package=THT]
  R2 = Resistor [tolerance=±5% resistance=10k package=THT]
  Bauteil1 = ws2812b [package="smd 2812b"]
  Bauteil2 = I2C level shifter bidirectional
  U1 = NodeMCU V1.0

nets:
  N1: R1.pin_0, R2.Pin_0, U1.A0
  N2: R1.pin_1, U1.3V3#19
  N3: R2.Pin_1, U1.GND#33
  VDD: Bauteil1.VDD, Bauteil2.HV, U1.Vin
  VSS: Bauteil1.VSS, Bauteil2.GND, U1.GND#16
  N4: Bauteil1.DIN, Bauteil2.HV1
  N5: Bauteil2.LV, Bauteil2.LV1, U1.D1, U1.RX, U1.3V3#14

custom parts:
  NodeMCU V1.0: ESP8266 based NodeMCU V1.0
